# Fritzing sketch pengukuran jarak (saved by Fritzing 0.9.3b)
breadboards: 1

parts:
  Part1 = Arduino Uno (Rev3)
  hc-sr1 = hc-sr04

nets:
  GND: Part1.D9_PWM, Part1.D10_PWM/SS, Part1.GND, hc-sr1.Trig, hc-sr1.Echo, hc-sr1.GND
  5V: Part1.5V, hc-sr1.VCC
